// Logisim project ALU.circ as structural Verilog: 1 circuit, main circuit ALU
module ALU (
  input  CarryIn,
  input  [3:0] Codop,
  input  [31:0] A,
  input  [31:0] B,
  input  [4:0] Shift,
  output [31:0] S,
  output [3:0] Flags
);

  wire and_3_out, and_4_out, bitselector_1_out, bitselector_2_out, bitselector_3_out, C_1, C_2, not_2_out,
       xor_1_out, xor_2_out;
  wire [31:0] adder_1_out, adder_2_out, and_1_out, and_2_out, multiplexer_1_out, multiplier_1_out,
       negator_1_out, nor_1_out, not_1_out, or_1_out, shifter_1_out, shifter_2_out, shifter_3_out,
       shifter_4_out, subtractor_1_out, subtractor_2_out;

  assign not_1_out = ~B;  // NOT_Gate not_1, 32 bits wide
  not not_2 (not_2_out, CarryIn);
  assign or_1_out = B | A;  // OR_Gate or_1, 32 bits wide
  assign and_1_out = not_1_out & A;  // AND_Gate and_1, 32 bits wide
  assign and_2_out = B & A;  // AND_Gate and_2, 32 bits wide
  assign nor_1_out = ~(B | A);  // NOR_Gate nor_1, 32 bits wide
  Shifter #(.width(32)) shifter_1 (.in(B), .\dist (Shift), .out(shifter_1_out));
  Shifter #(.width(32), .shift("lr")) shifter_2 (.in(B), .\dist (Shift), .out(shifter_2_out));
  Shifter #(.width(32), .shift("ar")) shifter_3 (.in(B), .\dist (Shift), .out(shifter_3_out));
  Adder #(.width(32)) adder_1 (.a(A), .b(B), .out(adder_1_out), .cin(CarryIn), .cout(C_1));
  Subtractor #(.width(32)) subtractor_1 (.a(B), .b(A), .out(subtractor_1_out), .bin(not_2_out));  // open: bout
  Shifter #(.width(32), .shift("rr")) shifter_4 (.in(B), .\dist (Shift), .out(shifter_4_out));
  Negator #(.width(32)) negator_1 (.in(A), .out(negator_1_out));
  Subtractor #(.width(32)) subtractor_2 (.a(B), .b(A), .out(subtractor_2_out), .bin(1'b0));  // open: bout
  Adder #(.width(32)) adder_2 (.a(B), .b(A), .out(adder_2_out), .cin(1'b0), .cout(C_2));
  Multiplier #(.width(32)) multiplier_1 (.a(B), .b(A), .out(multiplier_1_out), .cin({32{1'b0}}));  // open: cout
  Multiplexer #(.select(4), .width(32), .enable("false")) multiplexer_1 (
    .in0(and_2_out), .in1(nor_1_out), .in2(shifter_1_out), .in3(shifter_2_out), .in4(shifter_3_out),
    .in5(adder_1_out), .in6(subtractor_1_out), .in7(shifter_4_out), .in8(and_2_out), .in9(negator_1_out),
    .in10(subtractor_2_out), .in11(adder_2_out), .in12(or_1_out), .in13(multiplier_1_out), .in14(and_1_out),
    .in15(not_1_out), .out(multiplexer_1_out), .sel(Codop));
  Multiplexer #(.select(4), .enable("false")) multiplexer_2 (
    .in0(1'b0), .in1(1'b0), .in2(1'b0), .in3(1'b0), .in4(1'b0), .in5(C_1), .in6(1'b0), .in7(1'b0),
    .in8(1'b0), .in9(1'b0), .in10(1'b0), .in11(C_2), .in12(1'b0), .in13(1'b0), .in14(1'b0), .in15(1'b0),
    .out(Flags[2]), .sel(Codop));
  Multiplexer #(.select(4), .enable("false")) multiplexer_3 (
    .in0(1'b0), .in1(1'b0), .in2(1'b0), .in3(1'b0), .in4(1'b0), .in5(and_3_out), .in6(and_4_out), .in7(1'b0),
    .in8(1'b0), .in9(1'b0), .in10(1'b0), .in11(and_3_out), .in12(and_4_out), .in13(1'b0), .in14(1'b0),
    .in15(1'b0), .out(Flags[3]), .sel(Codop));
  BitSelector #(.width(32)) bitselector_1 (.in(multiplexer_1_out), .out(bitselector_1_out), .sel({5{1'b1}}));
  Multiplexer #(.select(4), .width(32), .enable("false")) multiplexer_4 (
    .in0(multiplexer_1_out), .in1(multiplexer_1_out), .in2(multiplexer_1_out), .in3(multiplexer_1_out),
    .in4(multiplexer_1_out), .in5(multiplexer_1_out), .in6(multiplexer_1_out), .in7(multiplexer_1_out),
    .in8(B), .in9(multiplexer_1_out), .in10(B), .in11(B), .in12(multiplexer_1_out), .in13(multiplexer_1_out),
    .in14(multiplexer_1_out), .in15(multiplexer_1_out), .out(S), .sel(Codop));
  Comparator #(.width(32)) comparator_1 (
    .a(multiplexer_1_out), .b({32{1'b0}}), .eq(Flags[1]), .lt(Flags[0]));  // open: gt
  BitSelector #(.width(32)) bitselector_2 (.in(B), .out(bitselector_2_out), .sel({5{1'b1}}));
  BitSelector #(.width(32)) bitselector_3 (.in(A), .out(bitselector_3_out), .sel({5{1'b1}}));
  xor xor_1 (xor_1_out, bitselector_2_out, bitselector_3_out);
  xor xor_2 (xor_2_out, bitselector_3_out, bitselector_1_out);
  and and_3 (and_3_out, ~xor_1_out, xor_2_out);  // AND_Gate
  and and_4 (and_4_out, xor_1_out, ~xor_2_out);  // AND_Gate

  // Other names for the same wires on the sheet: N = Flags[0]; Z = Flags[1]; C = Flags[2]; V = Flags[3]

  // Notes on the sheet:
  //   Discard result for opcode 1000 (TST)
  //   1010 (CMP) and 1011 (CMN)
  //   effectively copying Rn to Rd
endmodule
