// Logisim project Controller.circ as structural Verilog: 1 circuit, main circuit Controller
module Controller (
  input  [15:0] Inst,
  input  [3:0] FlagsIn,
  input  Reset,
  input  [31:0] R0,
  input  [31:0] R1,
  input  [31:0] R2,
  input  [31:0] R3,
  input  [31:0] R4,
  input  [31:0] R5,
  input  [31:0] R6,
  input  [31:0] R7,
  input  [31:0] RAM_Value,
  input  Clk,
  output Carry,
  output DP_Shift,
  output Imm32_Enable,
  output [4:0] Imm5,
  output [31:0] Imm32,
  output [3:0] ALU_Opcode,
  output [2:0] Rm,
  output [2:0] Rn,
  output [2:0] Rd,
  output [3:0] Flags,
  output [31:0] RAM_Addr,
  output Load,
  output Store,
  output PC_Hold,
  output [2:0] Mask,
  output [31:0] SP,
  output [31:0] PC
);

  wire and_3_out, and_4_out, and_5_out, and_6_out, and_7_out, and_8_out, and_9_out, and_10_out, and_11_out,
       and_12_out, and_14_out, and_15_out, and_16_out, and_17_out, bitselector_1_out, comparator_1_eq,
       comparator_2_eq, comparator_3_eq, comparator_4_eq, comparator_5_eq, comparator_6_eq, comparator_7_eq,
       comparator_8_eq, comparator_9_eq, comparator_10_eq, conditional_1_verified,
       load_address_1_imm32_enable, load_store_1_p18, load_store_1_p19, load_store_1_p20, not_1_out,
       not_2_out, not_3_out, not_4_out, opcode_decoder_1_conditional, opcode_decoder_1_data_processing,
       opcode_decoder_1_high_register_op, opcode_decoder_1_load_address, opcode_decoder_1_load_store,
       opcode_decoder_1_long_branch, opcode_decoder_1_shift, opcode_decoder_1_signextend,
       opcode_decoder_1_sp_address, or_2_out, or_3_out, or_5_out, or_6_out, or_8_out, or_10_out, or_11_out,
       or_12_out, or_13_out, or_14_out, or_16_out, or_19_out, pull_resistor_1_node,
       shift_add_sub_mov_1_carry, shift_add_sub_mov_1_imm32_enable, sp_address_1_write_enable, t_ff_1_q,
       t_ff_1_qn;
  wire [2:0] controlled_buffer_3_out, data_processing_1_rd, data_processing_1_rm, data_processing_1_rn,
       load_address_1_rd, load_store_1_p16, multiplexer_8_out, or_7_out, or_18_out, pull_resistor_4_node,
       pull_resistor_6_node, pull_resistor_18_node, shift_add_sub_mov_1_rd, shift_add_sub_mov_1_rm,
       shift_add_sub_mov_1_rn;
  wire [3:0] controlled_buffer_7_out, controlled_buffer_10_out, counter_1_q, data_processing_1_alu_opcode,
       data_processing_1_flags_update_mask, load_address_1_alu_opcode, or_4_out, or_15_out,
       pull_resistor_7_node, shift_add_sub_mov_1_alu_opcode, shift_add_sub_mov_1_flags_update_mask,
       subtractor_4_out;
  wire [3:3] multiplexer_8_out_2;
  wire [7:0] multiplexer_2_out;
  wire [10:0] conditional_1_offset, or_9_out, pull_resistor_3_node;
  wire [31:0] adder_1_out, adder_2_out, adder_3_out, adder_4_out, adder_5_out, adder_6_out, adder_7_out,
       adder_8_out, and_2_out, and_13_out, bit_extender_1_out, bit_extender_2_out, bit_extender_3_out,
       bit_extender_4_out, bit_extender_5_out, controlled_buffer_13_out, controlled_buffer_14_out,
       load_address_1_imm32, load_store_1_p17, load_store_1_p21, LR_Value, multiplexer_1_out,
       multiplexer_3_out, multiplexer_4_out, multiplexer_5_out, multiplexer_6_out, multiplexer_7_out,
       multiplexer_10_out, multiplexer_11_out, multiplier_1_out, negator_1_out, negator_2_out, or_1_out,
       or_17_out, or_20_out, or_32_out, pull_resistor_2_node, pull_resistor_8_node, pull_resistor_9_node,
       pull_resistor_12_node, pull_resistor_13_node, pull_resistor_14_node, pull_resistor_15_node,
       pull_resistor_19_node, pull_resistor_20_node, register_1_q, shift_add_sub_mov_1_imm32,
       sp_address_1_new_stack_pointer, subtractor_1_out, subtractor_2_out, subtractor_3_out;
  wire [31:8] multiplexer_2_out_2;

  assign or_1_out = pull_resistor_2_node | sp_address_1_new_stack_pointer;  // OR_Gate or_1, 32 bits wide
  Register #(.width(32)) Stack_Pointer (.D(or_1_out), .en(or_2_out), .clk(Clk), .Q(SP), .clr(Reset));
  or or_2 (or_2_out, sp_address_1_write_enable, pull_resistor_1_node);
  Opcode_Decoder opcode_decoder_1 (
    .Opcode(Inst[15:9]), .Shift(opcode_decoder_1_shift), .Load_Store(opcode_decoder_1_load_store),
    .SP_Address(opcode_decoder_1_sp_address), .Conditional(opcode_decoder_1_conditional),
    .Load_Address(opcode_decoder_1_load_address), .Long_Branch(opcode_decoder_1_long_branch),
    .High_Register_Op(opcode_decoder_1_high_register_op), .Data_Processing(opcode_decoder_1_data_processing),
    .SignExtend(opcode_decoder_1_signextend));
  Pull_Resistor pull_resistor_1 (.node(pull_resistor_1_node));
  Pull_Resistor pull_resistor_2 (.node(pull_resistor_2_node));
  assign pull_resistor_2_node = pull_resistor_1_node ? multiplexer_3_out : 32'bz;  // Controlled_Buffer controlled_buffer_1
  Adder #(.width(32)) adder_1 (.a(PC), .b(32'h4), .out(adder_1_out));  // open: cin, cout
  T_Flip_Flop #(.trigger("falling")) t_ff_1 (
    .T(and_10_out), .clk(Clk), .Q(t_ff_1_q), .Qn(t_ff_1_qn), .reset(not_1_out));  // open: preset
  and and_1 (pull_resistor_1_node, or_3_out, and_10_out, comparator_8_eq);
  assign and_2_out = adder_1_out & ~32'h2;  // AND_Gate and_2, 32 bits wide
  or or_3 (or_3_out, t_ff_1_q, and_16_out);
  assign or_4_out = data_processing_1_flags_update_mask | shift_add_sub_mov_1_flags_update_mask;  // OR_Gate or_4, 4 bits wide
  Comparator #(.width(4)) comparator_1 (.a(Inst[9:6]), .b(4'b1101), .eq(comparator_1_eq));  // open: gt, lt
  Comparator #(.width(4)) comparator_2 (.a(Inst[9:6]), .b(4'b1000), .eq(comparator_2_eq));  // open: gt, lt
  Comparator #(.width(4)) comparator_3 (.a(Inst[9:6]), .b(4'b1001), .eq(comparator_3_eq));  // open: gt, lt
  Comparator #(.width(4)) comparator_4 (.a(Inst[9:6]), .b(4'b0001), .eq(comparator_4_eq));  // open: gt, lt
  Comparator #(.width(4)) comparator_5 (.a(Inst[9:6]), .b(4'b1010), .eq(comparator_5_eq));  // open: gt, lt
  Comparator #(.width(4)) comparator_6 (.a(Inst[9:6]), .b(4'b0010), .eq(comparator_6_eq));  // open: gt, lt
  Comparator #(.width(4)) comparator_7 (.a(Inst[9:6]), .b(4'b1110), .eq(comparator_7_eq));  // open: gt, lt
  or or_5 (or_5_out, t_ff_1_q, ~and_10_out);  // OR_Gate
  Pull_Resistor pull_resistor_3 (.node(pull_resistor_3_node));
  assign pull_resistor_3_node = opcode_decoder_1_long_branch ? Inst[10:0] : 11'bz;  // Controlled_Buffer controlled_buffer_2
  and and_3 (and_3_out, comparator_1_eq, opcode_decoder_1_high_register_op);
  and and_4 (and_4_out, comparator_2_eq, opcode_decoder_1_high_register_op);
  or or_6 (or_6_out, and_4_out, or_19_out, and_5_out);
  assign controlled_buffer_3_out = or_6_out ? Inst[2:0] : 3'bz;  // Controlled_Buffer controlled_buffer_3
  Pull_Resistor pull_resistor_4 (.node(pull_resistor_4_node));
  assign pull_resistor_4_node = and_4_out ? Inst[5:3] : 3'bz;  // Controlled_Buffer controlled_buffer_4
  and and_5 (and_5_out, comparator_3_eq, opcode_decoder_1_high_register_op);
  and and_6 (and_6_out, comparator_4_eq, opcode_decoder_1_high_register_op);
  and and_7 (and_7_out, comparator_5_eq, opcode_decoder_1_high_register_op);
  and and_8 (and_8_out, comparator_6_eq, opcode_decoder_1_high_register_op);
  and and_9 (and_9_out, comparator_7_eq, opcode_decoder_1_high_register_op);
  Comparator #(.width(6)) comparator_8 (
    .a({Inst[15:12], Inst[10:9]}), .b(6'b101110), .eq(comparator_8_eq));  // open: gt, lt
  BitSelector #(.width(9)) bitselector_1 (
    .in(Inst[8:0]), .out(bitselector_1_out), .sel({multiplexer_8_out_2[3], multiplexer_8_out}));
  Conditional conditional_1 (
    .Offset(conditional_1_offset), .Verified(conditional_1_verified), .Instruction(Inst), .Z(Flags[2]),
    .C(Flags[1]), .N(Flags[3]), .V(Flags[0]), .Enable(opcode_decoder_1_conditional));
  Pull_Resistor pull_resistor_5 (.node(controlled_buffer_3_out));
  assign or_7_out = pull_resistor_4_node | pull_resistor_6_node;  // OR_Gate or_7, 3 bits wide
  Pull_Resistor pull_resistor_6 (.node(pull_resistor_6_node));
  assign pull_resistor_6_node = or_19_out ? controlled_buffer_3_out : 3'bz;  // Controlled_Buffer controlled_buffer_5
  Pull_Resistor pull_resistor_7 (.node(pull_resistor_7_node));
  assign pull_resistor_7_node = and_4_out ? 4'b0010 : 4'bz;  // Controlled_Buffer controlled_buffer_6
  Multiplexer #(.select(3), .width(32)) multiplexer_1 (
    .in5(SP), .in6(LR_Value), .in7(and_2_out), .out(multiplexer_1_out), .sel(Inst[5:3]));  // open: in0, in1, in2, in3, in4
  or or_8 (or_8_out, or_13_out, and_17_out);
  Multiplexer #(.select(3), .width(32)) multiplexer_2 (
    .in0(R0), .in1(R1), .in2(R2), .in3(R3), .in4(R4), .in5(R5), .in6(R6), .in7(R7),
    .out({multiplexer_2_out_2, multiplexer_2_out}), .sel(Inst[5:3]));
  assign bit_extender_1_out = {{24{multiplexer_2_out[7]}}, multiplexer_2_out};  // Bit_Extender bit_extender_1
  assign bit_extender_2_out = {{24{1'b0}}, multiplexer_2_out};  // Bit_Extender bit_extender_2
  Counter #(.max('hf), .width(4)) counter_1 (
    .clr(not_1_out), .count(or_5_out), .clk(Clk), .Q(counter_1_q));  // open: load, up, D, carry
  not not_1 (not_1_out, comparator_8_eq);
  and and_10 (and_10_out, bitselector_1_out, comparator_8_eq);
  Subtractor #(.width(32)) subtractor_1 (.a(SP), .b(32'h4), .out(subtractor_1_out));  // open: bin, bout
  Adder #(.width(32)) adder_2 (.a(SP), .b(32'h4), .out(adder_2_out));  // open: cin, cout
  Shift_Add_Sub_Mov shift_add_sub_mov_1 (
    .Flags_Update_Mask(shift_add_sub_mov_1_flags_update_mask), .Carry(shift_add_sub_mov_1_carry),
    .Imm32_Enable(shift_add_sub_mov_1_imm32_enable), .Rm(shift_add_sub_mov_1_rm),
    .Rn(shift_add_sub_mov_1_rn), .Rd(shift_add_sub_mov_1_rd), .Imm5(Imm5), .Imm32(shift_add_sub_mov_1_imm32),
    .ALU_Opcode(shift_add_sub_mov_1_alu_opcode), .Instruction(Inst), .Enable(opcode_decoder_1_shift));
  Data_Processing data_processing_1 (
    .Rn(data_processing_1_rn), .Rm(data_processing_1_rm), .ALU_Opcode(data_processing_1_alu_opcode),
    .Flags_Update_Mask(data_processing_1_flags_update_mask), .Rd(data_processing_1_rd), .Instruction(Inst),
    .Enable(opcode_decoder_1_data_processing));
  Flags_APSR flags_apsr_1 (.Update_Mask(or_4_out), .Flags_In(FlagsIn), .Clk(Clk), .Rst(Reset), .Flags_Out(Flags));
  // Load_Store load_store_1: pin names not known; wires that end beside it: Inst, opcode_decoder_1_load_store, SP, Clk, Reset, R0, R1, R2, R3, R4, R5, R6, R7, PC, RAM_Value, load_store_1_p16, load_store_1_p17, load_store_1_p18, load_store_1_p19, load_store_1_p20, load_store_1_p21, Mask
  Load_Address load_address_1 (
    .Enable(opcode_decoder_1_load_address), .Instruction(Inst), .Program_Counter(PC), .Stack_Pointer(SP),
    .Imm32_Enable(load_address_1_imm32_enable), .Rd(load_address_1_rd),
    .ALU_Opcode(load_address_1_alu_opcode), .Imm32(load_address_1_imm32));
  assign bit_extender_3_out = {{21{or_9_out[10]}}, or_9_out};  // Bit_Extender bit_extender_3
  assign or_9_out = conditional_1_offset | pull_resistor_3_node;  // OR_Gate or_9, 11 bits wide
  or or_10 (or_10_out, conditional_1_verified, and_3_out, and_9_out, opcode_decoder_1_long_branch, or_8_out);
  Adder #(.width(32)) adder_3 (.a(PC), .b(32'h2), .out(adder_3_out));  // open: cin, cout
  Register #(.width(32)) Link_Register (.D(adder_3_out), .en(or_11_out), .clk(Clk), .Q(LR_Value));  // open: clr
  or or_11 (or_11_out, opcode_decoder_1_long_branch, and_9_out);
  assign controlled_buffer_7_out = or_12_out ? 4'b1001 : 4'bz;  // Controlled_Buffer controlled_buffer_7
  or or_12 (or_12_out, and_5_out, opcode_decoder_1_signextend);
  Pull_Resistor pull_resistor_8 (.node(pull_resistor_8_node));
  assign pull_resistor_8_node = and_5_out ? negator_1_out : 32'bz;  // Controlled_Buffer controlled_buffer_8
  Negator #(.width(32)) negator_1 (.in(multiplexer_1_out), .out(negator_1_out));
  Pull_Resistor pull_resistor_9 (.node(pull_resistor_9_node));
  assign pull_resistor_9_node = and_6_out ? multiplexer_1_out : 32'bz;  // Controlled_Buffer controlled_buffer_9
  assign controlled_buffer_10_out = and_6_out ? 4'b0101 : 4'bz;  // Controlled_Buffer controlled_buffer_10
  or or_13 (or_13_out, and_7_out, and_8_out);
  Subtractor #(.width(32)) subtractor_2 (
    .a({multiplexer_2_out_2, multiplexer_2_out}), .b(32'h1), .out(subtractor_2_out));  // open: bin, bout
  Adder #(.width(32)) adder_4 (
    .a({multiplexer_2_out_2, multiplexer_2_out}), .b(PC), .out(adder_4_out));  // open: cin, cout
  assign bit_extender_4_out = {{16{multiplexer_2_out_2[15]}}, {multiplexer_2_out_2[15:8], multiplexer_2_out}};  // Bit_Extender bit_extender_4
  assign bit_extender_5_out = {{16{1'b0}}, {multiplexer_2_out_2[15:8], multiplexer_2_out}};  // Bit_Extender bit_extender_5
  Multiplexer #(.width(32)) multiplexer_3 (
    .in0(subtractor_1_out), .in1(adder_2_out), .out(multiplexer_3_out), .sel(Inst[11]));
  SP_Address sp_address_1 (
    .New_Stack_Pointer(sp_address_1_new_stack_pointer), .Write_Enable(sp_address_1_write_enable),
    .Stack_Pointer(SP), .Instruction(Inst), .Enable(opcode_decoder_1_sp_address));
  Adder #(.width(32)) adder_5 (.a(32'h2), .b(bit_extender_3_out), .out(adder_5_out));  // open: cin, cout
  or or_14 (or_14_out, conditional_1_verified, opcode_decoder_1_long_branch);
  Pull_Resistor pull_resistor_10 (.node(controlled_buffer_7_out));
  assign or_15_out = controlled_buffer_7_out | controlled_buffer_10_out;  // OR_Gate or_15, 4 bits wide
  or or_16 (or_16_out, and_5_out, or_19_out);
  assign or_17_out = pull_resistor_8_node | pull_resistor_13_node | pull_resistor_9_node;  // OR_Gate or_17, 32 bits wide
  Pull_Resistor pull_resistor_11 (.node(controlled_buffer_10_out));
  Adder #(.width(32)) adder_6 (.a(adder_4_out), .b(32'h4), .out(adder_6_out));  // open: cin, cout
  Multiplexer #(.width(32)) multiplexer_4 (
    .in0({multiplexer_2_out_2, multiplexer_2_out}), .in1(multiplexer_1_out), .out(multiplexer_4_out),
    .sel(Inst[6]));
  Multiplexer #(.select(2), .width(32)) multiplexer_5 (
    .in0(bit_extender_4_out), .in1(bit_extender_1_out), .in2(bit_extender_5_out), .in3(bit_extender_2_out),
    .out(multiplexer_5_out), .sel(Inst[7:6]));
  not not_2 (not_2_out, Inst[11]);
  and and_11 (and_11_out, and_10_out, ~and_17_out, Inst[11]);  // AND_Gate
  Subtractor #(.width(32)) subtractor_3 (.a(SP), .b(32'h4), .out(subtractor_3_out));  // open: bin, bout
  and and_12 (and_12_out, and_10_out, ~Inst[11]);  // AND_Gate
  assign or_18_out = load_store_1_p16 | pull_resistor_18_node;  // OR_Gate or_18, 3 bits wide
  Multiplier #(.width(32)) multiplier_1 (.a(32'h2), .b(adder_5_out), .out(multiplier_1_out));  // open: cin, cout
  Adder #(.width(32)) adder_7 (.a(multiplier_1_out), .b(PC), .out(adder_7_out), .cin(1'b0));  // open: cout
  or or_19 (or_19_out, and_6_out, opcode_decoder_1_signextend);
  Multiplexer #(.width(32)) multiplexer_6 (
    .in0(subtractor_2_out), .in1(and_13_out), .out(multiplexer_6_out), .sel(and_8_out));
  assign and_13_out = ~32'h1 & adder_6_out;  // AND_Gate and_13, 32 bits wide
  Pull_Resistor pull_resistor_12 (.node(pull_resistor_12_node));
  assign pull_resistor_12_node = and_9_out ? multiplexer_4_out : 32'bz;  // Controlled_Buffer controlled_buffer_11
  Pull_Resistor pull_resistor_13 (.node(pull_resistor_13_node));
  assign pull_resistor_13_node = opcode_decoder_1_signextend ? negator_2_out : 32'bz;  // Controlled_Buffer controlled_buffer_12
  Negator #(.width(32)) negator_2 (.in(multiplexer_5_out), .out(negator_2_out));
  Subtractor #(.width(4)) subtractor_4 (.a(4'b1000), .b(counter_1_q), .out(subtractor_4_out));  // open: bin, bout
  assign controlled_buffer_13_out = comparator_8_eq ? multiplexer_7_out : 32'bz;  // Controlled_Buffer controlled_buffer_13
  Multiplexer #(.width(32)) multiplexer_7 (.in0(subtractor_3_out), .in1(SP), .out(multiplexer_7_out), .sel(Inst[11]));
  // Probe on multiplexer_7_out
  and and_14 (and_14_out, opcode_decoder_1_shift, ~opcode_decoder_1_data_processing);  // AND_Gate
  not not_3 (not_3_out, PC_Hold);
  assign controlled_buffer_14_out = or_14_out ? adder_7_out : 32'bz;  // Controlled_Buffer controlled_buffer_14
  Pull_Resistor pull_resistor_14 (.node(pull_resistor_14_node));
  assign pull_resistor_14_node = and_3_out ? LR_Value : 32'bz;  // Controlled_Buffer controlled_buffer_15
  assign or_20_out = pull_resistor_15_node | pull_resistor_12_node;  // OR_Gate or_20, 32 bits wide
  Pull_Resistor pull_resistor_15 (.node(pull_resistor_15_node));
  assign pull_resistor_15_node = or_13_out ? multiplexer_6_out : 32'bz;  // Controlled_Buffer controlled_buffer_16
  Comparator #(.width(4)) comparator_9 (.a(counter_1_q), .b(4'b1001), .eq(comparator_9_eq));  // open: gt, lt
  Multiplexer #(.width(4)) multiplexer_8 (
    .in0(counter_1_q), .in1(subtractor_4_out), .out({multiplexer_8_out_2[3], multiplexer_8_out}),
    .sel(not_2_out));
  Pull_Resistor pull_resistor_16 (.node(controlled_buffer_13_out));
  Multiplexer multiplexer_9 (.in0(Flags[1]), .in1(shift_add_sub_mov_1_carry), .out(Carry), .sel(and_14_out));
  Pull_Resistor pull_resistor_17 (.node(controlled_buffer_14_out));
  not not_4 (not_4_out, or_10_out);
  and and_15 (and_15_out, comparator_8_eq, ~and_16_out, ~comparator_9_eq);  // AND_Gate
  Pull_Resistor pull_resistor_18 (.node(pull_resistor_18_node));
  assign pull_resistor_18_node = and_10_out ? multiplexer_8_out : 3'bz;  // Controlled_Buffer controlled_buffer_17
  or or_21 (DP_Shift, and_14_out, opcode_decoder_1_high_register_op);
  or or_22 (Imm32_Enable, shift_add_sub_mov_1_imm32_enable, or_16_out, load_address_1_imm32_enable);
  assign Imm32 = shift_add_sub_mov_1_imm32 | load_store_1_p21 | pull_resistor_19_node | load_address_1_imm32 | or_17_out;  // OR_Gate or_23, 32 bits wide
  assign ALU_Opcode = shift_add_sub_mov_1_alu_opcode | data_processing_1_alu_opcode | or_15_out | load_address_1_alu_opcode | pull_resistor_7_node;  // OR_Gate or_24, 4 bits wide
  assign Rm = shift_add_sub_mov_1_rm | data_processing_1_rm | or_18_out;  // OR_Gate or_25, 3 bits wide
  assign Rn = shift_add_sub_mov_1_rn | data_processing_1_rn | or_18_out | or_7_out;  // OR_Gate or_26, 3 bits wide
  assign Rd = shift_add_sub_mov_1_rd | data_processing_1_rd | controlled_buffer_3_out | or_18_out | load_address_1_rd;  // OR_Gate or_27, 3 bits wide
  assign RAM_Addr = load_store_1_p17 | controlled_buffer_13_out;  // OR_Gate or_28, 32 bits wide
  or or_29 (Load, load_store_1_p18, and_11_out);
  or or_30 (Store, load_store_1_p19, and_12_out);
  or or_31 (PC_Hold, load_store_1_p20, and_15_out);
  assign or_32_out = {32{1'b0}} | controlled_buffer_14_out | pull_resistor_14_node | or_20_out | pull_resistor_20_node;  // OR_Gate or_32, 32 bits wide
  Adder #(.width(32)) adder_8 (.a(PC), .b(32'h2), .out(adder_8_out));  // open: cin, cout
  Multiplexer #(.select(4), .width(32)) multiplexer_10 (
    .in0(R0), .in1(R1), .in2(R2), .in3(R3), .in4(R4), .in5(R5), .in6(R6), .in7(R7), .in8(LR_Value),
    .out(multiplexer_10_out), .sel({multiplexer_8_out_2[3], multiplexer_8_out}));  // open: in9, in10, in11, in12, in13, in14, in15
  Counter #(.max('hffffffff), .trigger("falling"), .width(32)) counter_2 (
    .clr(Reset), .load(not_3_out), .count(1'b0), .clk(Clk), .D(multiplexer_11_out), .Q(PC));  // open: up, carry
  Multiplexer #(.width(32)) multiplexer_11 (
    .in0(or_32_out), .in1(adder_8_out), .out(multiplexer_11_out), .sel(not_4_out));
  and and_16 (and_16_out, t_ff_1_qn, and_17_out);
  Comparator #(.width(4)) comparator_10 (
    .a(4'b1000), .b({multiplexer_8_out_2[3], multiplexer_8_out}), .eq(comparator_10_eq));  // open: gt, lt
  and and_17 (and_17_out, comparator_10_eq, Inst[11], comparator_8_eq);
  Pull_Resistor pull_resistor_19 (.node(pull_resistor_19_node));
  assign pull_resistor_19_node = and_12_out ? multiplexer_10_out : 32'bz;  // Controlled_Buffer controlled_buffer_18
  Register #(.width(32)) register_1 (.D(RAM_Value), .en(and_17_out), .clk(Clk), .Q(register_1_q), .clr(not_1_out));
  Pull_Resistor pull_resistor_20 (.node(pull_resistor_20_node));
  assign pull_resistor_20_node = and_17_out ? register_1_q : 32'bz;  // Controlled_Buffer controlled_buffer_19

  // Other names for the same wires on the sheet: PC_Value[31:0] = PC; SP_Value[31:0] = SP

  // Notes on the sheet:
  //   Extract carry
  //   Extract Opcode
  //   0=push(store), 1=pop(load)
  //   regs[i]
  //   IF Reg_Imm=1 THEN use shift value from register ELSE use shift value from Imm5
  //   Buffer flags for next instruction
  //   Add 3 to offset because ARM pre-increments PC
  //   and does an additional prefetch operation
endmodule
