// Logisim project Ctl_Load_Address.circ as structural Verilog: 1 circuit, main circuit Load_Address
module Load_Address (
  input  Enable,
  input  [15:0] Instruction,
  input  [15:0] Program_Counter,
  input  [31:0] Stack_Pointer,
  output Imm32_Enable,
  output [2:0] Rd,
  output [3:0] ALU_Opcode,
  output [31:0] Imm32
);

  wire [15:0] controlled_buffer_1_out;
  wire [31:0] adder_1_out, bit_extender_1_out, bit_extender_2_out, multiplexer_1_out, negator_1_out;

  assign {controlled_buffer_1_out[15:11], Rd, controlled_buffer_1_out[7:0]} = Enable ? Instruction : 16'bz;  // Controlled_Buffer controlled_buffer_1
  Pull_Resistor pull_resistor_1 (.node({controlled_buffer_1_out[15:11], Rd, controlled_buffer_1_out[7:0]}));
  assign bit_extender_1_out = {{16{1'b0}}, Program_Counter};  // Bit_Extender bit_extender_1
  assign bit_extender_2_out = {{24{1'b0}}, controlled_buffer_1_out[7:0]};  // Bit_Extender bit_extender_2
  Multiplexer #(.width(32)) multiplexer_1 (
    .in0(bit_extender_1_out), .in1(Stack_Pointer), .out(multiplexer_1_out), .sel(controlled_buffer_1_out[11]));
  Adder #(.width(32)) adder_1 (.a(bit_extender_2_out), .b(multiplexer_1_out), .out(adder_1_out));  // open: cin, cout
  assign ALU_Opcode = Enable ? 4'b1001 : 4'bz;  // Controlled_Buffer controlled_buffer_2
  assign Imm32 = Enable ? negator_1_out : 32'bz;  // Controlled_Buffer controlled_buffer_3
  Negator #(.width(32)) negator_1 (.in(adder_1_out), .out(negator_1_out));
  Pull_Resistor pull_resistor_2 (.node(ALU_Opcode));
  Pull_Resistor pull_resistor_3 (.node(Imm32));

  assign Imm32_Enable = Enable;
endmodule
