// Logisim project Ctl_Load_Store.circ as structural Verilog: 1 circuit, main circuit Load_Store
module Load_Store (
  input  [15:0] Instruction,
  input  [31:0] R0,
  input  Enable,
  input  [31:0] R1,
  input  Clk,
  input  [31:0] R2,
  input  Reset,
  input  [31:0] R3,
  input  [31:0] R4,
  input  [31:0] R5,
  input  [31:0] R6,
  input  [31:0] R7,
  input  [31:0] Stack_Pointer,
  input  [31:0] Program_Counter,
  input  [31:0] Old_Value,
  output [31:0] Imm32,
  output [2:0] Rmd,
  output Store,
  output Load,
  output PC_Hold,
  output [31:0] RAM_Addr
);

  wire and_1_out, and_2_out, and_3_out, and_4_out, and_6_out, and_7_out, and_8_out, d_ff_1_q, d_ff_1_qn,
       or_1_out, or_2_out, or_3_out, or_4_out;
  wire [2:0] t;
  wire [31:0] adder_1_out, adder_2_out, adder_3_out, adder_4_out, adder_5_out, and_5_out, and_9_out,
       bit_extender_1_out, bit_extender_2_out, multiplexer_4_out, multiplexer_6_out, multiplexer_7_out,
       multiplexer_8_out, multiplexer_9_out, multiplexer_10_out, multiplier_1_out, multiplier_2_out, Rb, Ro,
       Rt;

  Multiplexer #(.select(3), .width(32)) multiplexer_1 (
    .in0(R0), .in1(R1), .in2(R2), .in3(R3), .in4(R4), .in5(R5), .in6(R6), .in7(R7), .out(Rb),
    .sel(Instruction[5:3]));
  Multiplexer #(.select(3), .width(32)) multiplexer_2 (
    .in0(R0), .in1(R1), .in2(R2), .in3(R3), .in4(R4), .in5(R5), .in6(R6), .in7(R7), .out(Ro),
    .sel(Instruction[8:6]));
  Multiplexer #(.select(3), .width(32)) multiplexer_3 (
    .in0(R0), .in1(R1), .in2(R2), .in3(R3), .in4(R4), .in5(R5), .in6(R6), .in7(R7), .out(Rt), .sel(t));
  assign bit_extender_1_out = {{24{1'b0}}, Instruction[7:0]};  // Bit_Extender bit_extender_1
  or or_1 (or_1_out, Instruction[11], and_1_out);
  and and_1 (and_1_out, Instruction[9], Instruction[10], ~Instruction[11], ~Instruction[13], Instruction[14], ~Instruction[15]);  // AND_Gate
  Adder #(.width(32)) adder_1 (.a(Program_Counter), .b(32'h4), .out(adder_1_out));  // open: cin, cout
  and and_2 (and_2_out, ~Instruction[15], Instruction[14], Instruction[13], ~Instruction[11], Instruction[10], ~Instruction[9]);  // AND_Gate
  and and_3 (and_3_out, ~Instruction[15], Instruction[14], Instruction[13], Instruction[12], ~Instruction[11]);  // AND_Gate
  buf and_4 (and_4_out, ~d_ff_1_q);  // AND_Gate AND_Gate
  assign and_5_out = adder_1_out & ~32'h2;  // AND_Gate and_5, 32 bits wide
  Multiplier #(.width(32)) multiplier_1 (.a(bit_extender_1_out), .b(32'h4), .out(multiplier_1_out));  // open: cin, cout
  Shifter #(.shift("lr"), .width(32)) shifter_1 (.\dist (5'b00010));  // open: in, out
  assign bit_extender_2_out = {{27{1'b0}}, Instruction[10:6]};  // Bit_Extender bit_extender_2
  Adder #(.width(32)) adder_2 (.a(bit_extender_1_out), .b(Stack_Pointer), .out(adder_2_out), .cin(1'b0));  // open: cout
  or or_2 (or_2_out, and_2_out, and_3_out);
  and and_6 (and_6_out, Instruction[12], ~Instruction[14]);  // AND_Gate
  and and_7 (and_7_out, ~Instruction[12], ~Instruction[13], ~Instruction[15]);  // AND_Gate
  D_Flip_Flop #(.trigger("falling")) d_ff_1 (
    .D(and_4_out), .clk(Clk), .Q(d_ff_1_q), .Qn(d_ff_1_qn), .reset(or_3_out));  // open: preset
  or or_3 (or_3_out, ~1'b1, Reset, ~Enable);  // OR_Gate
  Adder #(.width(32)) adder_3 (.a(and_5_out), .b(multiplier_1_out), .out(adder_3_out));  // open: cin, cout
  Multiplexer #(.width(32)) multiplexer_4 (
    .in0(adder_3_out), .in1(adder_4_out), .out(multiplexer_4_out), .sel(Instruction[12]));
  Adder #(.width(32)) adder_4 (.a(Rb), .b(Ro), .out(adder_4_out));  // open: cin, cout
  Multiplier #(.width(32)) multiplier_2 (.a(bit_extender_2_out), .b(32'h4), .out(multiplier_2_out));  // open: cin, cout
  or or_4 (or_4_out, and_6_out, and_7_out);
  Multiplexer #(.width(3)) multiplexer_5 (.in0(Instruction[2:0]), .in1(Instruction[10:8]), .out(t), .sel(or_4_out));
  Adder #(.width(32)) adder_5 (.a(Rb), .b(multiplier_2_out), .out(adder_5_out));  // open: cin, cout
  buf and_8 (and_8_out, d_ff_1_qn);  // AND_Gate
  Multiplexer #(.width(32)) multiplexer_6 (
    .in0(multiplexer_4_out), .in1(multiplexer_7_out), .out(multiplexer_6_out), .sel(Instruction[13]));
  Multiplexer #(.width(32)) multiplexer_7 (.in0(adder_5_out), .in1(Rb), .out(multiplexer_7_out), .sel(Instruction[12]));
  assign and_9_out = Rt & 32'hff;  // AND_Gate and_9, 32 bits wide
  and and_10 (Store, ~or_1_out, d_ff_1_q, Enable);  // AND_Gate
  and and_11 (Load, Enable, or_1_out, d_ff_1_q);
  and and_12 (PC_Hold, Enable, and_8_out);
  Multiplexer #(.width(32)) multiplexer_8 (
    .in1(adder_2_out), .out(multiplexer_8_out), .sel(Instruction[12]));  // open: in0
  Multiplexer #(.width(32)) multiplexer_9 (.in0(Rt), .in1(and_9_out), .out(multiplexer_9_out), .sel(or_2_out));
  assign RAM_Addr = Enable ? multiplexer_10_out : 32'bz;  // Controlled_Buffer controlled_buffer_1
  Multiplexer #(.width(32)) multiplexer_10 (
    .in0(multiplexer_6_out), .in1(multiplexer_8_out), .out(multiplexer_10_out), .sel(Instruction[15]));
  Pull_Resistor pull_resistor_1 (.node(Imm32));
  assign Imm32 = Enable ? multiplexer_9_out : 32'bz;  // Controlled_Buffer controlled_buffer_2
  Pull_Resistor pull_resistor_2 (.node(Rmd));
  assign Rmd = Enable ? t : 3'bz;  // Controlled_Buffer controlled_buffer_3
  Pull_Resistor pull_resistor_3 (.node(RAM_Addr));

  // Other names for the same wires on the sheet: b[2:0] = Instruction[5:3]; o[2:0] = Instruction[8:6];
  //   Old[31:0] = Old_Value

  // Notes on the sheet:
  //   Instruction: pull=down
  //   Delay load and hold PC for 1 cycle for the RAM to send out requested data 
endmodule
