// Logisim project Machine.circ as structural Verilog: 2 circuits, main circuit main
module main (
  output Clk,
  output DO
);

  wire and_1_out, BancRegistre_1_p6, BancRegistre_1_p7, BancRegistre_1_p8, BancRegistre_1_p9,
       BancRegistre_1_p11, BancRegistre_1_p12, BancRegistre_1_p13, clock_1_out, comparator_1_lt, CPU_1_store,
       or_1_out, Rst;
  wire [7:0] RAM_Addr, ROM_Addr;
  wire [8:8] VMEM;
  wire [15:0] ROMa_data;
  wire [31:0] BancRegistre_1_p14, CPU_1_r0, CPU_1_r1, CPU_1_r2, CPU_1_r3, CPU_1_r4, CPU_1_r5, CPU_1_r6,
       CPU_1_r7, CPU_1_ram_out, multiplexer_1_out, RAMa_dout;
  wire [31:2] BancRegistre_1_p4;

  RAM #(.dataWidth(32), .databus("bibus")) RAMa (
    .addr(RAM_Addr), .we(and_1_out), .oe(1'b1), .clk(clock_1_out), .din(CPU_1_ram_out), .dout(RAMa_dout));
  and and_1 (and_1_out, CPU_1_store, comparator_1_lt);
  // Probe on {VMEM[8], RAM_Addr}
  Comparator #(.width(9), .mode("unsigned")) comparator_1 (
    .a({VMEM[8], RAM_Addr}), .b(9'h100), .lt(comparator_1_lt));  // open: gt, eq
  or or_1 (or_1_out, ~CPU_1_store, comparator_1_lt);  // OR_Gate
  Multiplexer #(.width(32), .enable("false")) multiplexer_1 (
    .in0(CPU_1_ram_out), .in1(BancRegistre_1_p14), .out(multiplexer_1_out), .sel(or_1_out));
  Clock clock_1 (.out(clock_1_out));
  // Probe on BancRegistre_1_p7
  // Probe on BancRegistre_1_p6
  // Probe on {BancRegistre_1_p4, DO, Clk}
  LED A0 (.in(RAMa_dout[0]));
  LED A1 (.in(RAMa_dout[1]));
  LED A2 (.in(RAMa_dout[2]));
  ROM #(.dataWidth(16)) ROMa (.addr(ROM_Addr), .data(ROMa_data));
  // Probe on BancRegistre_1_p8
  // Probe on BancRegistre_1_p12
  // Probe on BancRegistre_1_p11
  // Probe on BancRegistre_1_p9
  Button Rst_Button (.out(Rst));
  LED A3 (.in(RAMa_dout[3]));
  LED A4 (.in(RAMa_dout[4]));
  LED A5 (.in(RAMa_dout[5]));
  // Probe on BancRegistre_1_p13
  // BancRegistre BancRegistre_1: pin names not known; wires that end beside it: multiplexer_1_out, RAM_Addr[2:0], clock_1_out, {BancRegistre_1_p4, DO, Clk}, Rst, BancRegistre_1_p6, BancRegistre_1_p7, BancRegistre_1_p8, BancRegistre_1_p9, RAM_Addr[2:0], BancRegistre_1_p11, BancRegistre_1_p12, BancRegistre_1_p13, BancRegistre_1_p14
  LED A6 (.in(RAMa_dout[6]));
  LED A7 (.in(RAMa_dout[7]));
  LED L0 (.in(CPU_1_r0[0]));
  // Probe on CPU_1_r1
  // Probe on CPU_1_r0
  LED L3 (.in(CPU_1_r0[3]));
  LED L1 (.in(CPU_1_r0[1]));
  LED L2 (.in(CPU_1_r0[2]));
  // Probe on CPU_1_r3
  // Probe on CPU_1_r2
  // Probe on CPU_1_r5
  // Probe on CPU_1_r4
  LED L4 (.in(CPU_1_r0[4]));
  LED L5 (.in(CPU_1_r0[5]));
  // Probe on CPU_1_r7
  // Probe on CPU_1_r6
  CPU CPU_1 (
    .ROM_Addr(ROM_Addr), .RAM_In(RAMa_dout), .Rst(Rst), .RAM_Addr({VMEM[8], RAM_Addr}), .ROM_In(ROMa_data),
    .Clk(clock_1_out), .RAM_Out(CPU_1_ram_out), .R0(CPU_1_r0), .R1(CPU_1_r1), .R2(CPU_1_r2), .R3(CPU_1_r3),
    .R4(CPU_1_r4), .R5(CPU_1_r5), .R6(CPU_1_r6), .R7(CPU_1_r7), .Store(CPU_1_store));
  LED L6 (.in(CPU_1_r0[6]));
  LED L7 (.in(CPU_1_r0[7]));
  LED LED_10 (.in(DO));
  LED LED_1 (.in(RAM_Addr[0]));
  LED LED_2 (.in(RAM_Addr[1]));
  LED LED_3 (.in(RAM_Addr[2]));
  LED LED_9 (.in(Clk));
  LED LED_4 (.in(RAM_Addr[3]));
  LED LED_5 (.in(RAM_Addr[4]));
  LED LED_6 (.in(RAM_Addr[5]));
  LED LED_7 (.in(RAM_Addr[6]));
  LED LED_8 (.in(RAM_Addr[7]));

  // Other names for the same wires on the sheet: VMEM[7:0] = RAM_Addr

  // Notes on the sheet:
  //   contents of ROMa (hex, n*v repeats v):
  //   b0b4 2000 9030 21ff 209 912c 21ff 9128 9024 9020 2110 911c 210c 9118 9014 2108 9110 9034 defe 2000
  //   900c defe 980c 991c 4288 da0f defe 2000 9024 9820 2101 1a08 9020 9820 9924 49 1840 9034 defe 980c
  //   1c40 900c dee9 2000 9008 defe 9808 9918 4288 da22 defe 982c 9014 2000 9004 defe 9804 991c 4288 da13
  //   defe 9814 2101 4008 9024 9820 1a08 9020 9820 9924 49 1840 9034 9814 1040 9014 defe 9804 1c40 9004
  //   dee5 defe 9808 1c40 9008 ded6 2000 9000 defe 9800 9910 4288 da10 defe 9824 2101 1a08 9024 9820 1a08
  //   9020 9820 9924 49 1840 9034 defe 9800 1c40 9000 dee8 982c 1c40 902c 982c 200 9928 4288 dd02 defe
  //   2000 902c defe de95
  //   Use only 8 bit adresses
endmodule

module CPU (
  input  [31:0] RAM_In,
  input  [15:0] ROM_In,
  input  Clk,
  input  Rst,
  output [7:0] ROM_Addr,
  output [8:0] RAM_Addr,
  output [31:0] R3,
  output [31:0] R7,
  output [31:0] RAM_Out,
  output [31:0] R2,
  output [31:0] R6,
  output [31:0] R1,
  output [31:0] R5,
  output [31:0] R0,
  output [31:0] R4,
  output Store
);

  wire Controller_1_carry, Controller_1_dp_shift, Controller_1_imm32_enable, Controller_1_load;
  wire [2:0] Controller_1_rd, Controller_1_rm, Controller_1_rn;
  wire [3:0] ALU_1_flags, Controller_1_alu_opcode;
  wire [4:0] Controller_1_imm5, multiplexer_3_out;
  wire [31:0] ALU_1_s, Controller_1_imm32, multiplexer_1_out, multiplexer_2_out, Regs_1_p15;

  Controller Controller_1 (
    .Inst(ROM_In), .Rm(Controller_1_rm), .PC(ROM_Addr), .ALU_Opcode(Controller_1_alu_opcode),
    .Imm5(Controller_1_imm5), .Rn(Controller_1_rn), .Flags(ALU_1_flags),
    .Imm32_Enable(Controller_1_imm32_enable), .Rd(Controller_1_rd), .Imm32(Controller_1_imm32),
    .DP_Shift(Controller_1_dp_shift), .Carry(Controller_1_carry), .RAM_Addr(RAM_Addr),
    .Load(Controller_1_load), .Store(Store), .Clk(Clk), .Reset(Rst));
  Multiplexer #(.width(32), .enable("false")) multiplexer_1 (
    .in0(ALU_1_s), .in1(RAM_In), .out(multiplexer_1_out), .sel(Controller_1_load));
  // BancRegistre Regs_1: pin names not known; wires that end beside it: multiplexer_1_out, Controller_1_rd, Clk, R0, Rst, R1, R2, R3, R4, Controller_1_rm, R5, R6, Controller_1_rn, R7, Regs_1_p15, RAM_Out
  Multiplexer #(.width(32), .enable("false")) multiplexer_2 (
    .in0(RAM_Out), .in1(Controller_1_imm32), .out(multiplexer_2_out), .sel(Controller_1_imm32_enable));
  Multiplexer #(.width(5), .enable("false")) multiplexer_3 (
    .in0(multiplexer_2_out[4:0]), .in1(Controller_1_imm5), .out(multiplexer_3_out),
    .sel(Controller_1_dp_shift));
  ALU ALU_1 (
    .S(ALU_1_s), .Flags(ALU_1_flags), .A(multiplexer_2_out), .B(Regs_1_p15), .Shift(multiplexer_3_out),
    .CarryIn(Controller_1_carry), .Codop(Controller_1_alu_opcode));
  // Probe on ALU_1_flags

  // Notes on the sheet:
  //   RAM/ALU Input selector
  //   Use data frpm Imm8 instead of A register
  //   Use data from register or immediate for shift
  //   Trigger carry for additionner
  //   Imm8 input for Move
endmodule
