// Logisim project Machine_Logisim3.circ as structural Verilog: 3 circuits, main circuit Facade
module Facade (
);

  wire and_1_out, and_2_out, and_3_out, and_4_out, and_5_out, and_6_out, BREAK, Clk, Clk_Button2,
       Clk_Button_out, clock_1_out, CONTINUE, counter_1_carry, CPU_1_pc_hold, d_ff_4_qn, d_ff_5_qn,
       decoder_1_out0, decoder_1_out1, decoder_1_out2, decoder_1_out3, decoder_1_out4, decoder_1_out5,
       decoder_1_out6, decoder_2_out1, KEYB_Eof, KEYB_Read, KEYB_ReadEn, MMIO_En, or_1_out, or_2_out, RAM_En,
       Reset, RGB_Upd, RNG_Read, Rst_Button_out, RST_Signal, Store, Toggle, TTY_Upd;
  wire [1:0] comparator_1_eq;
  wire [3:0] binary_to_bcd_converter_1_p2, binary_to_bcd_converter_1_p3, binary_to_bcd_converter_1_p4,
       binary_to_bcd_converter_1_p5, CPU_1_flags;
  wire [4:0] counter_1_q, counter_2_q, JOY_X, JOY_Y;
  wire [6:0] KEYB_Char, TTY_Char;
  wire [15:0] bit_extender_1_out, bit_extender_6_out, INSTR, register_8_q;
  wire [29:0] subtractor_1_out;
  wire [31:0] bcd8digits_1_bcd, bit_extender_2_out, bit_extender_3_out, bit_extender_4_out, CODE_Addr,
       CPU_1_r0, CPU_1_r1, CPU_1_r6, CPU_1_sp, DATA_Addr, DATA_Out, Dip1, Dip2, Dip3, divider_1_out,
       divider_1_rem, MEM_Addr, MEM_Out, MMIO_Out, R2, R3, R4, R5, R7, RAM_Out, RAMa_dout, random_1_out,
       register_3_q, Res, RGB_Color, ROM_Out, Screen;
  wire [31:1] undriven_2;
  wire [31:5] undriven_4, undriven_5;
  wire [31:7] undriven, undriven_3;

  Subtractor #(.width(30)) subtractor_1 (.a(MEM_Addr[31:2]), .b(30'h4000), .out(subtractor_1_out));  // open: bin, bout
  DipSwitch dipswitch_1 (
    .sw1(Dip1[7]), .sw2(Dip1[6]), .sw3(Dip1[5]), .sw4(Dip1[4]), .sw5(Dip1[3]), .sw6(Dip1[2]), .sw7(Dip1[1]),
    .sw8(Dip1[0]));
  Multiplexer #(.width(32)) multiplexer_1 (.in0(CODE_Addr), .in1(DATA_Addr), .out(MEM_Addr), .sel(Toggle));
  RAM #(.addrWidth(16), .asyncread("true"), .dataWidth(32)) RAMa (
    .addr(bit_extender_1_out), .we(and_1_out), .oe(1'b1), .clk(Clk), .din(DATA_Out), .dout(RAMa_dout));
  Bit_Extender #(.in_width(30), .\type ("zero")) bit_extender_1 (.in(subtractor_1_out), .out(bit_extender_1_out));
  and and_1 (and_1_out, Store, RAM_En);
  // Probe on Dip1[7:0]
  DipSwitch dipswitch_2 (
    .sw1(Dip2[7]), .sw2(Dip2[6]), .sw3(Dip2[5]), .sw4(Dip2[4]), .sw5(Dip2[3]), .sw6(Dip2[2]), .sw7(Dip2[1]),
    .sw8(Dip2[0]));
  Decoder #(.select(4)) decoder_1 (
    .out0(decoder_1_out0), .out1(decoder_1_out1), .out2(decoder_1_out2), .out3(decoder_1_out3),
    .out4(decoder_1_out4), .out5(decoder_1_out5), .out6(decoder_1_out6), .sel(MEM_Addr[5:2]), .en(and_2_out));  // open: out7, out8, out9, out10, out11, out12, out13, out14, out15
  Comparator #(.width(16)) comparator_1 (.a(MEM_Addr[31:16]), .b({16{1'b0}}), .eq(comparator_1_eq[0]));  // open: gt, lt
  Comparator #(.width(28)) comparator_2 (
    .a({MEM_Addr[31:6], MEM_Addr[1:0]}), .b(28'hffffffc), .eq(comparator_1_eq[1]));  // open: gt, lt
  // Probe on Dip2[7:0]
  and and_2 (and_2_out, MMIO_En, Store);
  // Probe on MEM_Addr[5:2]
  Decoder #(.enable("false"), .select(2)) decoder_2 (
    .out0(RAM_En), .out1(decoder_2_out1), .out2(MMIO_En), .sel(comparator_1_eq));  // open: out3
  Multiplexer #(.select(2), .width(32)) multiplexer_2 (
    .in0(RAM_Out), .in1(ROM_Out), .in2(MMIO_Out), .out(MEM_Out), .sel(comparator_1_eq));  // open: in3
  // Probe on MEM_Out
  DipSwitch dipswitch_3 (
    .sw1(Dip3[7]), .sw2(Dip3[6]), .sw3(Dip3[5]), .sw4(Dip3[4]), .sw5(Dip3[3]), .sw6(Dip3[2]), .sw7(Dip3[1]),
    .sw8(Dip3[0]));
  // Probe on Dip3[7:0]
  Register #(.trigger("falling"), .width(7)) register_1 (
    .D(DATA_Out[6:0]), .en(decoder_1_out0), .clk(Clk), .Q(TTY_Char), .clr(Reset));
  Register #(.width(32)) register_2 (.D(DATA_Out), .en(decoder_1_out1), .clk(Clk), .Q(Res), .clr(Reset));
  Register #(.width(32)) register_3 (.D(DATA_Out), .en(decoder_1_out2), .clk(Clk), .Q(register_3_q), .clr(Reset));
  Register #(.width(1)) register_4 (.D(DATA_Out[0]), .en(decoder_1_out4), .clk(Clk), .Q(RST_Signal), .clr(Reset));
  Register #(.width(1)) register_5 (.D(DATA_Out[0]), .en(decoder_1_out5), .clk(Clk), .Q(BREAK), .clr(or_1_out));
  or or_1 (or_1_out, Reset, CONTINUE);
  Register #(.trigger("falling"), .width(32)) register_6 (
    .D(DATA_Out), .en(decoder_1_out6), .clk(Clk), .Q(RGB_Color), .clr(Reset));
  assign bit_extender_2_out = {{8{1'b0}}, RAMa_dout[31:8]};  // Bit_Extender bit_extender_2
  assign bit_extender_3_out = {{16{1'b0}}, RAMa_dout[31:16]};  // Bit_Extender bit_extender_3
  assign bit_extender_4_out = {{24{1'b0}}, RAMa_dout[31:24]};  // Bit_Extender bit_extender_4
  Counter #(.max('h1f), .width(5)) counter_1 (
    .clk(Clk), .carry(counter_1_carry), .Q(counter_1_q));  // open: clr, load, up, count, D
  DotMatrix #(.inputtype("row"), .matrixcols(8), .matrixrows(4)) dotmatrix_1 (
    .row0(Screen[7:0]), .row1(Screen[15:8]), .row2(Screen[23:16]), .row3(Screen[31:24]));
  Joystick #(.bits(5)) joystick_1 (.x(JOY_X), .y(JOY_Y));
  D_Flip_Flop d_ff_1 (.D(decoder_1_out0), .clk(Clk), .Q(TTY_Upd));  // open: Qn, preset, reset
  Register #(.width(32)) register_7 (.D(register_3_q), .en(and_3_out), .clk(Clk), .Q(Screen), .clr(Reset));
  and and_3 (and_3_out, DATA_Out[0], decoder_1_out3);
  D_Flip_Flop d_ff_2 (.D(decoder_1_out6), .clk(Clk), .Q(RGB_Upd));  // open: Qn, preset, reset
  Multiplexer #(.select(2), .width(32)) multiplexer_3 (
    .in0(RAMa_dout), .in1(bit_extender_2_out), .in2(bit_extender_3_out), .in3(bit_extender_4_out),
    .out(RAM_Out), .sel(MEM_Addr[1:0]));
  // ROM #(.addrWidth(16), .line("quad"), .misaligned("true")) ROMa: pin names not known
  Bit_Extender #(.in_width(32), .\type ("zero")) bit_extender_5 (.in(MEM_Addr));  // open: out
  Counter #(.max('h1f), .width(5)) counter_2 (
    .count(counter_1_carry), .clk(Clk), .Q(counter_2_q));  // open: clr, load, up, D, carry
  // RGB_Video #(.cursor("No Cursor"), .height(32), .scale(6), .width(32)) rgb_video_1: pin names not known; wires that end beside it: Clk, RGB_Upd
  Clock clock_1 (.out(clock_1_out));
  and and_4 (and_4_out, clock_1_out, ~BREAK);  // AND_Gate
  Button Rst_Button (.out(Rst_Button_out));
  DotMatrix #(.inputtype("row"), .matrixcols(32), .matrixrows(1)) dotmatrix_2 (.row0(Res));
  Hex_Digit_Display hex_digit_display_1 (.value(Res[15:12]));  // open: dp
  Hex_Digit_Display hex_digit_display_2 (.value(Res[11:8]));  // open: dp
  D_Flip_Flop d_ff_3 (.D(KEYB_Read), .clk(Clk), .Q(KEYB_ReadEn), .reset(or_2_out));  // open: Qn, preset
  or or_2 (or_2_out, ~KEYB_Read, Reset);  // OR_Gate
  or or_3 (Clk, and_4_out, Clk_Button_out, Clk_Button2);
  Button Clk_Button (.out(Clk_Button_out));
  Bit_Extender #(.in_width(32), .\type ("zero")) bit_extender_6 (.in(MEM_Out), .out(bit_extender_6_out));
  Hex_Digit_Display hex_digit_display_3 (.value(Res[7:4]));  // open: dp
  Hex_Digit_Display hex_digit_display_4 (.value(Res[3:0]));  // open: dp
  or or_4 (Reset, Rst_Button_out, RST_Signal);
  Register #(.width(16)) register_8 (
    .D(bit_extender_6_out), .en(d_ff_4_qn), .clk(Clk), .Q(register_8_q), .clr(RST_Signal));
  D_Flip_Flop #(.trigger("falling")) d_ff_4 (
    .D(CPU_1_pc_hold), .clk(Clk), .Q(Toggle), .Qn(d_ff_4_qn), .reset(RST_Signal));  // open: preset
  // RGB_Video #(.cursor("No Cursor"), .height(32), .scale(4), .width(32)) rgb_video_2: pin names not known; wires that end beside it: Clk, 1'b1, counter_1_q, counter_2_q, INSTR
  Button button_1 (.out(CONTINUE));
  // Binary_to_BCD_converter #(.binvalue(13)) binary_to_bcd_converter_1: pin names not known; wires that end beside it: Res[12:0], binary_to_bcd_converter_1_p2, binary_to_bcd_converter_1_p3, binary_to_bcd_converter_1_p4, binary_to_bcd_converter_1_p5
  D_Flip_Flop #(.trigger("falling")) d_ff_5 (.D(1'b0), .clk(Clk), .Qn(d_ff_5_qn), .preset(Reset));  // open: Q, reset
  // Probe on ROM_Out
  Button button_2 (.out(Clk_Button2));
  // Probe on Res
  // Probe on Res
  Hex_Digit_Display hex_digit_display_5 (.value(binary_to_bcd_converter_1_p3));  // open: dp
  Hex_Digit_Display hex_digit_display_6 (.value(binary_to_bcd_converter_1_p2));  // open: dp
  Random #(.width(32)) random_1 (.next(RNG_Read), .clk(Clk), .out(random_1_out));  // open: clr
  and and_5 (and_5_out, Clk, d_ff_5_qn);
  Multiplexer #(.width(16)) multiplexer_4 (.in0(bit_extender_6_out), .in1(register_8_q), .out(INSTR), .sel(Toggle));
  // Probe on INSTR
  Hex_Digit_Display hex_digit_display_7 (.value(binary_to_bcd_converter_1_p4));  // open: dp
  Hex_Digit_Display hex_digit_display_8 (.value(binary_to_bcd_converter_1_p5));  // open: dp
  BCD8digits bcd8digits_1 (.BCD(bcd8digits_1_bcd), .Number(Res));
  Divider #(.width(32)) divider_1 (.a(R2), .b(R3), .out(divider_1_out), .rem(divider_1_rem));  // open: upper
  // Probe on R3
  // Probe on R2
  // Probe on CPU_1_r1
  // Probe on CPU_1_r0
  TTY #(.cols(50), .rows(20)) tty_1 (.data(TTY_Char), .clk(Clk), .we(TTY_Upd), .clr(Reset));
  // Probe on R7
  // Probe on CPU_1_r6
  // Probe on R5
  // Probe on R4
  Multiplexer #(.select(4), .width(32)) multiplexer_5 (
    .in0({undriven, TTY_Char}), .in1(Res), .in2(register_3_q), .in3(Dip1), .in4(Dip2), .in5(Dip3),
    .in6({undriven_2, KEYB_Eof}), .in7({undriven_3, KEYB_Char}), .in8({undriven_5, JOY_X}),
    .in9({undriven_4, JOY_Y}), .in10(random_1_out), .in11(bcd8digits_1_bcd), .in12(divider_1_out),
    .in13(divider_1_rem), .out(MMIO_Out), .sel(MEM_Addr[5:2]));  // open: in14, in15
  // Probe on CPU_1_flags
  CPU CPU_1 (
    .Flags(CPU_1_flags), .SP(CPU_1_sp), .RAM_Out(DATA_Out), .PC_Hold(CPU_1_pc_hold), .ROM_Addr(CODE_Addr),
    .Store(Store), .RAM_Addr(DATA_Addr), .R0(CPU_1_r0), .R1(CPU_1_r1), .R2(R2), .R3(R3), .R4(R4), .R5(R5),
    .R6(CPU_1_r6), .R7(R7), .RAM_In(MEM_Out), .ROM_In(INSTR), .Clk(and_5_out), .Reset(Reset));
  Keyboard #(.buflen(128)) keyboard_1 (.clk(Clk), .re(KEYB_Read), .clr(Reset), .avail(KEYB_Eof), .data(KEYB_Char));
  and and_6 (and_6_out, ~Store, MMIO_En);  // AND_Gate
  Decoder #(.select(4)) decoder_3 (
    .out7(KEYB_Read), .out10(RNG_Read), .sel(MEM_Addr[5:2]), .en(and_6_out));  // open: out0, out1, out2, out3, out4, out5, out6, out8, out9, out11, out12, out13, out14, out15
  Pull_Resistor pull_resistor_1 (.node(MMIO_Out));
  // Probe on DATA_Addr
  // Probe on DATA_Out
  // Probe on CPU_1_sp
  // Probe on CODE_Addr

  // Other names for the same wires on the sheet: MMIO_Addr[3:0] = MEM_Addr[5:2]

  // Notes on the sheet:
  //   Entrées / Sorties mappées en mémoire
  //   Sorties
  //   contents of ROMa (hex, n*v repeats v):
  //   ae e2 10 b5 51 43 43 43 c9 18 3 c 14 c 63 43 c9 18 3 c 80 b2 92 b2 53 43 44 43 50 43 0 22 1b 19 52
  //   41 12 4 89 18 1a 4 1b c 80 18 59 41 10 bd d0 b5 2 af 1 68 0 29 f d0 42 68 c1 68 8b 0 9a 18 12 1f 0
  //   29 8 d0 49 1e c1 60 13 1f 11 24 24 4 12 68 a2 42 1a 46 f4 d1 d0 bd 80 b5 0 af 1 68 1 29 2 d1 0 1d ff
  //   f7 e2 ff 80 bd 80 b5 0 af 1 68 2 29 1 d0 ff f7 da ff 80 bd f0 b5 3 af 87 b0 4 46 86 68 14 20 70 43
  //   21 68 45 18 14 3d 2 a8 0 1d 1 90 0 2e e d0 76 1e a6 60 2 a8 14 22 29 46 0 f0 e6 f9 2 98 3 28 c d0 2
  //   a8 ff f7 d3 ff 14 3d ee e7 0 20 1 99 8 60 48 60 88 60 c8 60 3 20 2 90 2 a8 ff f7 c6 ff 7 b0 f0 bd f0
  //   b5 3 af 1 46 2 68 40 68 82 42 6 d0 50 1c 8 60 10 78 43 b2 0 2b 3 d4 f0 bd 11 20 0 4 f0 bd 93 1c b 60
  //   55 78 3f 24 25 40 1f 23 3 40 df 28 11 d9 d6 1c e 60 96 78 26 40 ad 1 ad 19 f0 28 c d3 10 1d 8 60 d0
  //   78 20 40 a9 1 8 18 59 7 c9 a 40 18 f0 bd 98 1 40 19 f0 bd 18 3 28 18 f0 bd b0 b5 2 af 2 46 8b 0 0 20
  //   1 46 0 2b a d0 14 68 30 3c 9 2c 5 d8 a 25 4d 43 61 19 1b 1f 12 1d f3 e7 1 20 b0 bd 0 46 f8 b5 4 af 4
  //   68 41 68 0 20 15 4b 0 94 81 42 a d0 25 68 9 3d 17 2d 7 d8 1 26 ae 40 1e 42 3 d0 24 1d 40 1c f2 e7 8
  //   46 88 42 4 46 0 d3 c 46 8d 0 0 9a ad 18 2d 1f 81 42 9 d9 2e 68 9 3e 17 2e 6 d8 1 22 b2 40 1a 42 2 d0
  //   49 1e f2 e7 21 46 9 1a 80 0 0 9a 10 18 f8 bd 0 46 1b 0 80 0 b0 b5 2 af 4 46 40 68 0 28 9 d0 45 1c 40
  //   0 85 42 0 d8 5 46 29 1 20 68 0 f0 e7 f8 3 e0 10 20 0 f0 c1 f8 1 25 0 28 4 d0 20 60 4 34 25 60 4 34
  //   b0 bd 3f 20 c0 43 0 21 8 4a 6 29 3 d0 53 5c 3 60 49 1c f9 e7 0 21 5 4a b 29 3 d0 53 5c 3 60 49 1c f9
  //   e7 a 21 1 60 fe e7 68 18 0 0 3a 18 0 0 b0 b5 2 af d 46 4 46 40 68 0 28 9 d0 45 19 40 0 85 42 0 d8 5
  //   46 a9 0 20 68 0 f0 b2 f8 2 e0 a8 0 0 f0 8c f8 0 28 4 d0 20 60 4 34 25 60 4 34 b0 bd 3f 20 c0 43 0 21
  //   8 4a 6 29 3 d0 53 5c 3 60 49 1c f9 e7 0 21 5 4a b 29 3 d0 53 5c 3 60 49 1c f9 e7 a 21 1 60 fe e7 68
  //   18 0 0 3a 18 0 0 b0 b5 2 af 4 46 40 68 0 28 a d0 45 1c 40 0 85 42 0 d8 5 46 18 21 69 43 20 68 0 f0
  //   7e f8 3 e0 18 20 0 f0 58 f8 1 25 0 28 4 d0 20 60 4 34 25 60 4 34 b0 bd 3f 20 c0 43 0 21 9 4a 6 29 3
  //   d0 53 5c 3 60 49 1c f9 e7 0 21 6 4a b 29 3 d0 53 5c 3 60 49 1c f9 e7 a 21 1 60 fe e7 0 46 68 18 0 0
  //   3a 18 0 0 b0 b5 2 af 4 46 40 68 0 28 a d0 45 1c 40 0 85 42 0 d8 5 46 14 21 69 43 20 68 0 f0 48 f8 3
  //   e0 14 20 0 f0 22 f8 1 25 0 28 4 d0 20 60 4 34 25 60 4 34 b0 bd 3f 20 c0 43 0 21 9 4a 6 29 3 d0 53 5c
  //   3 60 49 1c f9 e7 0 21 6 4a b 29 3 d0 53 5c 3 60 49 1c f9 e7 a 21 1 60 fe e7 0 46 68 18 0 0 3a 18 0 0
  //   b0 b5 2 af 1 21 9 4 b 68 c0 1d c4 8 62 1c 1d 46 19 46 28 46 2d 68 a5 42 5 d8 45 68 9d 42 1 46 f7 d1
  //   0 20 b0 bd 95 42 1 d1 43 68 6 e0 ab 1a d4 0 3 51 3 19 44 68 5c 60 2 60 4b 60 8 30 b0 bd fe b5 6 af 0
  //   28 12 d0 4 46 5 46 8 3d 2a 68 c8 1d c0 8 43 1c 93 42 d d0 e d2 d0 1a d9 0 68 50 68 18 21 1f 9 68 41
  //   60 2b 60 3 e0 8 46 ff f7 c4 ff 4 46 20 46 fe bd 2 90 1 93 d0 0 2e 18 1 20 0 4 0 68 3 46 b3 42 3 d0
  //   5b 68 83 42 fa d1 e e0 30 68 80 18 2 9b 98 42 9 d9 1 98 86 1a f0 0 8 38 ff f7 a8 ff 28 68 80 19 28
  //   60 e0 e7 8 46 ff f7 a1 ff 29 68 49 0 49 1e 0 22 0 29 d6 d0 a3 58 83 50 49 1e 12 1d f8 e7 3f 20 c0 43
  //   0 21 9 4a 6 29 3 d0 53 5c 3 60 49 1c f9 e7 0 21 6 4a d 29 3 d0 53 5c 3 60 49 1c f9 e7 a 21 1 60 fe
  //   e7 0 46 68 18 0 0 5a 18 0 0 92 8 0 2a 5 d0 b 68 4 31 3 60 4 30 52 1e f7 e7 70 47 89 8 0 29 4 d0 0 22
  //   2 60 4 30 49 1e f8 e7 70 47 80 b5 0 af ff f7 f3 ff 80 bd 92 8 88 42 7 d2 0 2a 11 d0 b 68 4 31 3 60 4
  //   30 52 1e f7 e7 93 0 1b 1f c9 18 c0 18 0 2a 5 d0 b 68 3 60 9 1f 0 1f 52 1e f7 e7 70 47 d0 b5 2 af f
  //   22 d4 43 2 46 b 46 20 68 d0 bd 3f 20 c0 43 c1 6a 0 29 f d0 2 46 38 32 b 7 8 d1 52 1c 9 9 fa e7 f 23
  //   b 40 30 33 3 60 52 1c 9 9 0 2a f7 d1 70 47 30 21 1 60 70 47 f8 b5 4 af 4 46 3f 20 0 90 c5 43 a8 69 0
  //   28 fc d0 ee 69 a 2e 14 d0 30 a 1 d0 0 98 0 e0 f0 b2 28 60 61 68 a0 68 88 42 4 d1 1 21 20 46 ff f7 72
  //   fe a0 68 81 0 22 68 56 50 40 1c a0 60 e4 e7 a 20 28 60 f8 bd 80 b5 0 af 98 b0 ff b0 ff b0 82 b0 9c
  //   48 9d 49 81 60 0 24 4 60 1 46 8 31 41 60 1 1f 8 60 c0 60 f0 20 ff f7 f4 fe 0 28 0 d1 ff e0 1 94 a 94
  //   a 21 3 91 9 91 0 90 8 90 80 20 ff f7 e7 fe 3f 21 cc 43 0 28 0 d1 5 e1 20 21 6 91 c 91 b 90 1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
  //   Reprendre après un point d'arrêt
  //   Tic d'horloge
  //   Entrées
  //   PC effectif
endmodule

module CPU (
  input  [31:0] RAM_In,
  input  [15:0] ROM_In,
  input  Clk,
  input  Reset,
  output [31:0] R3,
  output [31:0] R7,
  output [31:0] R2,
  output [31:0] R6,
  output [31:0] R1,
  output [31:0] R5,
  output [31:0] R0,
  output [31:0] R4,
  output [31:0] RAM_Out,
  output [31:0] ROM_Addr,
  output [31:0] RAM_Addr,
  output Store,
  output [3:0] Flags,
  output [31:0] SP,
  output PC_Hold
);

  wire Controller_1_carry, Controller_1_dp_shift, Controller_1_imm32_enable, Controller_1_load;
  wire [2:0] Controller_1_mask, Controller_1_rd, Controller_1_rm, Controller_1_rn;
  wire [3:0] ALU_1_flags, Controller_1_alu_opcode;
  wire [4:0] Controller_1_imm5, multiplexer_4_out;
  wire [31:0] ALU_1_s, bit_extender_1_out, bit_extender_2_out, bit_extender_3_out, bit_extender_4_out,
       Controller_1_imm32, multiplexer_1_out, multiplexer_2_out, multiplexer_3_out, Regs_1_p15, Regs_1_p16;

  assign bit_extender_1_out = {{24{1'b0}}, RAM_In[7:0]};  // Bit_Extender bit_extender_1
  assign bit_extender_2_out = {{24{RAM_In[7]}}, RAM_In[7:0]};  // Bit_Extender bit_extender_2
  assign bit_extender_3_out = {{16{1'b0}}, RAM_In[15:0]};  // Bit_Extender bit_extender_3
  assign bit_extender_4_out = {{16{RAM_In[15]}}, RAM_In[15:0]};  // Bit_Extender bit_extender_4
  Controller Controller_1 (
    .SP(SP), .DP_Shift(Controller_1_dp_shift), .Imm32_Enable(Controller_1_imm32_enable),
    .Imm5(Controller_1_imm5), .Imm32(Controller_1_imm32), .ALU_Opcode(Controller_1_alu_opcode),
    .Rm(Controller_1_rm), .Rn(Controller_1_rn), .Rd(Controller_1_rd), .Flags(Flags),
    .Carry(Controller_1_carry), .RAM_Addr(RAM_Addr), .Load(Controller_1_load), .Store(Store),
    .PC_Hold(PC_Hold), .Mask(Controller_1_mask), .PC(ROM_Addr), .FlagsIn(ALU_1_flags), .Clk(Clk),
    .Reset(Reset), .R4(R4), .R5(R5), .R6(R6), .R7(R7), .RAM_Value(RAM_In), .R0(R0), .R1(R1), .R2(R2),
    .R3(R3), .Inst(ROM_In));
  Multiplexer #(.select(3), .width(32)) multiplexer_1 (
    .in0(RAM_In), .in1(bit_extender_1_out), .in2(bit_extender_3_out), .in5(bit_extender_2_out),
    .in6(bit_extender_4_out), .out(multiplexer_1_out), .sel(Controller_1_mask));  // open: in3, in4, in7
  Multiplexer #(.width(32)) multiplexer_2 (
    .in0(ALU_1_s), .in1(multiplexer_1_out), .out(multiplexer_2_out), .sel(Controller_1_load));
  // BancRegistre Regs_1: pin names not known; wires that end beside it: multiplexer_2_out, Controller_1_rd, Clk, R0, Reset, R1, R2, R3, R4, Controller_1_rm, R5, R6, Controller_1_rn, R7, Regs_1_p15, Regs_1_p16
  Multiplexer #(.width(32)) multiplexer_3 (
    .in0(Regs_1_p16), .in1(Controller_1_imm32), .out(multiplexer_3_out), .sel(Controller_1_imm32_enable));
  Multiplexer #(.width(5)) multiplexer_4 (
    .in0(Regs_1_p16[4:0]), .in1(Controller_1_imm5), .out(multiplexer_4_out), .sel(Controller_1_dp_shift));
  ALU ALU_1 (
    .Flags(ALU_1_flags), .S(ALU_1_s), .CarryIn(Controller_1_carry), .Codop(Controller_1_alu_opcode),
    .A(multiplexer_3_out), .B(Regs_1_p15), .Shift(multiplexer_4_out));
  Multiplexer #(.width(32)) multiplexer_5 (.in0(Regs_1_p16), .in1(Controller_1_imm32), .out(RAM_Out), .sel(Store));
endmodule

module BCD8digits (
  input  [31:0] Number,
  output [31:0] BCD
);

  wire [31:0] divider_1_out, divider_2_out, divider_3_out, divider_4_out, divider_5_out, divider_6_out,
       divider_7_out;
  wire [31:4] divider_1_rem, divider_2_rem, divider_3_rem, divider_4_rem, divider_5_rem, divider_6_rem,
       divider_7_rem, divider_8_rem;

  Divider #(.width(32)) divider_1 (
    .a(Number), .b(32'ha), .out(divider_1_out), .rem({divider_1_rem, BCD[31:28]}));  // open: upper
  Divider #(.width(32)) divider_2 (
    .a(divider_1_out), .b(32'ha), .out(divider_2_out), .rem({divider_2_rem, BCD[27:24]}));  // open: upper
  Divider #(.width(32)) divider_3 (
    .a(divider_2_out), .b(32'ha), .out(divider_3_out), .rem({divider_3_rem, BCD[23:20]}));  // open: upper
  Divider #(.width(32)) divider_4 (
    .a(divider_3_out), .b(32'ha), .out(divider_4_out), .rem({divider_4_rem, BCD[19:16]}));  // open: upper
  Divider #(.width(32)) divider_5 (
    .a(divider_4_out), .b(32'ha), .out(divider_5_out), .rem({divider_5_rem, BCD[15:12]}));  // open: upper
  Divider #(.width(32)) divider_6 (
    .a(divider_5_out), .b(32'ha), .out(divider_6_out), .rem({divider_6_rem, BCD[11:8]}));  // open: upper
  Divider #(.width(32)) divider_7 (
    .a(divider_6_out), .b(32'ha), .out(divider_7_out), .rem({divider_7_rem, BCD[7:4]}));  // open: upper
  Divider #(.width(32)) divider_8 (.a(divider_7_out), .b(32'ha), .rem({divider_8_rem, BCD[3:0]}));  // open: out, upper
  // Probe on BCD
endmodule
